// Digital circuit decode.dig as structural Verilog
module decode (
  input  RST,
  input  [7:0] DATA,
  input  clk,
  input  C,
  input  Z,
  input  N,
  input  V,
  output b_o,
  output sh_o,
  output sl_o,
  output mh_o,
  output ml_o,
  output off_o,
  output s_a,
  output alu_d,
  output mf_a,
  output aluf_d,
  output f_o,
  output NC,
  output b_i,
  output sh_i,
  output sl_i,
  output mh_i,
  output ml_i,
  output off_i,
  output sl,
  output sl_plus__plus,
  output ml,
  output f_i,
  output ml_plus__plus,
  output A_i,
  output A_o,
  output MREAD,
  output MWRITE,
  output pAh_o,
  output pAl_o,
  output pAh_i,
  output pAl_i,
  output pBc_plus__plus,
  output pBc_a,
  output pBh_o,
  output pBl_o,
  output pBh_i,
  output pBl_i,
  output pAc_plus__plus,
  output pAc_a,
  output [15:0] Address,
  output [3:0] ALU_op,
  output ALU_latch,
  output [7:0] DBG
);

  wire _7493_1_pin1, _74138_1_pin7, _74138_1_pin9, _74138_2_pin7, _74138_2_pin15, _74138_3_pin7,
       _74138_3_pin9, _74138_3_pin10, _74138_3_pin15, _74138_4_pin7, _74138_4_pin9, _74138_4_pin11,
       _74138_4_pin15, _74541_1_pin19, _74573_1_pin11, and_1_out, and_2_out, and_3_out, and_4_out, and_5_out,
       and_6_out, and_7_out, and_8_out, and_10_out, and_11_out, and_12_out, and_13_out, and_14_out,
       nor_1_out, nor_2_out, nor_3_out, nor_4_out, nor_5_out, nor_6_out, not_1_out, not_2_out, not_3_out,
       not_11_out, or_1_out, or_2_out, or_3_out, or_9_out, or_10_out, or_16_out, or_17_out;
  wire [2:0] _7493_1_pin8;
  wire [6:0] CONTROL_low_d;
  wire [7:0] CONTROL_high_d;

  _74573 _74573_1 (
    .pin1(1'b0), .pin2(DATA[0]), .pin3(DATA[1]), .pin4(DATA[2]), .pin5(DATA[3]), .pin6(DATA[4]),
    .pin7(DATA[5]), .pin8(DATA[6]), .pin9(DATA[7]), .pin10(1'b0), .pin11(_74573_1_pin11), .pin12(DBG[7]),
    .pin13(DBG[6]), .pin14(DBG[5]), .pin15(DBG[4]), .pin16(ALU_op[3]), .pin17(ALU_op[2]), .pin18(ALU_op[1]),
    .pin19(ALU_op[0]), .pin20(1'b1));
  not not_1 (not_1_out, C);
  not not_2 (not_2_out, Z);
  and and_1 (and_1_out, ALU_op[0], C);
  and and_2 (and_2_out, ALU_op[1], Z);
  and and_3 (and_3_out, ALU_op[2], not_1_out);
  and and_4 (and_4_out, ALU_op[3], not_2_out);
  or or_1 (or_1_out, and_1_out, and_2_out);
  or or_2 (or_2_out, and_3_out, and_4_out);
  or or_3 (or_3_out, and_5_out, RST);
  _7493 _7493_1 (
    .pin1(_7493_1_pin1), .pin2(or_3_out), .pin3(or_3_out), .pin5(1'b1), .pin8(_7493_1_pin8[1]),
    .pin9(_7493_1_pin8[0]), .pin10(1'b0), .pin11(_7493_1_pin8[2]), .pin12(_7493_1_pin1), .pin14(clk));  // open: pin4, pin6, pin7, pin13
  ROM #(.AddrBits(13), .isProgramMemory("true"), .Bits(8)) CONTROL_low (
    .A({1'b0, DBG[7:4], ALU_op, 1'b0, _7493_1_pin8}), .sel(1'b1), .D({ALU_latch, CONTROL_low_d}));
  ROM #(.AddrBits(13), .isProgramMemory("true"), .Bits(8)) CONTROL_high (
    .A({1'b0, DBG[7:4], ALU_op, 1'b0, _7493_1_pin8}), .sel(1'b1), .D(CONTROL_high_d));
  nor nor_1 (nor_1_out, or_1_out, or_2_out);
  and and_5 (and_5_out, ALU_latch, _7493_1_pin1);
  not not_3 (not_3_out, clk);
  and and_6 (and_6_out, not_3_out, _7493_1_pin1);
  and and_7 (and_7_out, CONTROL_low_d[5], and_6_out);
  and and_8 (and_8_out, CONTROL_low_d[6], and_6_out);
  and and_9 (A_i, CONTROL_high_d[0], and_6_out);
  and and_10 (and_10_out, CONTROL_high_d[3], and_6_out);
  _74541 _74541_1 (
    .pin1(1'b0), .pin2(ALU_op[0]), .pin3(ALU_op[1]), .pin4(ALU_op[2]), .pin5(ALU_op[3]), .pin6(DBG[4]),
    .pin7(1'b1), .pin8(1'b1), .pin9(1'b1), .pin10(1'b0), .pin11(Address[15]), .pin12(Address[14]),
    .pin13(Address[13]), .pin14(Address[12]), .pin15(Address[11]), .pin16(Address[10]), .pin17(Address[9]),
    .pin18(Address[8]), .pin19(_74541_1_pin19), .pin20(1'b1));
  _74541 _74541_2 (
    .pin1(1'b0), .pin2(1'b1), .pin3(1'b1), .pin4(1'b1), .pin5(1'b1), .pin6(1'b1), .pin7(1'b1), .pin8(1'b1),
    .pin9(1'b1), .pin10(1'b0), .pin11(Address[7]), .pin12(Address[6]), .pin13(Address[5]),
    .pin14(Address[4]), .pin15(Address[3]), .pin16(Address[2]), .pin17(Address[1]), .pin18(Address[0]),
    .pin19(_74541_1_pin19), .pin20(1'b1));
  _74138 _74138_1 (
    .pin1(CONTROL_low_d[0]), .pin2(CONTROL_low_d[1]), .pin3(CONTROL_low_d[2]), .pin4(1'b0), .pin5(1'b0),
    .pin6(CONTROL_low_d[3]), .pin7(_74138_1_pin7), .pin8(1'b0), .pin9(_74138_1_pin9), .pin10(off_o),
    .pin11(ml_o), .pin12(mh_o), .pin13(sl_o), .pin14(sh_o), .pin15(b_o), .pin16(1'b1));
  _74138 _74138_2 (
    .pin1(CONTROL_low_d[0]), .pin2(CONTROL_low_d[1]), .pin3(CONTROL_low_d[2]), .pin4(1'b0), .pin5(1'b0),
    .pin6(CONTROL_low_d[4]), .pin7(_74138_2_pin7), .pin8(1'b0), .pin9(_74541_1_pin19), .pin10(f_o),
    .pin11(aluf_d), .pin12(mf_a), .pin13(alu_d), .pin14(s_a), .pin15(_74138_2_pin15), .pin16(1'b1));
  _74138 _74138_3 (
    .pin1(CONTROL_low_d[0]), .pin2(CONTROL_low_d[1]), .pin3(CONTROL_low_d[2]), .pin4(1'b0), .pin5(1'b0),
    .pin6(and_7_out), .pin7(_74138_3_pin7), .pin8(1'b0), .pin9(_74138_3_pin9), .pin10(_74138_3_pin10),
    .pin11(ml_i), .pin12(mh_i), .pin13(sl_i), .pin14(sh_i), .pin15(_74138_3_pin15), .pin16(1'b1));
  _74138 _74138_4 (
    .pin1(CONTROL_low_d[0]), .pin2(CONTROL_low_d[1]), .pin3(CONTROL_low_d[2]), .pin4(1'b0), .pin5(1'b0),
    .pin6(and_8_out), .pin7(_74138_4_pin7), .pin8(1'b0), .pin9(_74138_4_pin9), .pin10(ml_plus__plus),
    .pin11(_74138_4_pin11), .pin12(ml), .pin13(sl_plus__plus), .pin14(sl), .pin15(_74138_4_pin15),
    .pin16(1'b1));
  not not_4 (_74573_1_pin11, _74138_4_pin15);
  not not_5 (b_i, _74138_3_pin15);
  not not_6 (off_i, _74138_3_pin10);
  not not_7 (f_i, _74138_4_pin11);
  not not_8 (A_o, CONTROL_high_d[1]);
  not not_9 (MREAD, CONTROL_high_d[2]);
  not not_10 (MWRITE, and_10_out);
  nor nor_2 (nor_2_out, _74138_4_pin7, nor_1_out);
  and and_11 (and_11_out, nor_6_out, nor_2_out);
  not not_11 (not_11_out, nor_2_out);
  and and_12 (and_12_out, nor_2_out, nor_5_out);
  nor nor_3 (nor_3_out, and_11_out, nor_4_out);
  nor nor_4 (nor_4_out, nor_3_out, and_12_out);
  and and_13 (and_13_out, nor_3_out, not_11_out);
  and and_14 (and_14_out, not_11_out, nor_4_out);
  nor nor_5 (nor_5_out, and_13_out, nor_6_out);
  nor nor_6 (nor_6_out, nor_5_out, and_14_out);
  or or_4 (pAh_o, nor_5_out, _74138_1_pin9);
  or or_5 (pAl_o, nor_5_out, _74138_1_pin7);
  or or_6 (pAh_i, nor_5_out, _74138_3_pin9);
  or or_7 (pAl_i, nor_5_out, _74138_3_pin7);
  or or_8 (pBc_plus__plus, nor_5_out, _74138_4_pin9);
  or or_9 (or_9_out, nor_5_out, _74138_2_pin15);
  or or_10 (or_10_out, nor_6_out, _74138_2_pin7);
  or or_11 (pBh_o, nor_6_out, _74138_1_pin9);
  or or_12 (pBl_o, nor_6_out, _74138_1_pin7);
  or or_13 (pBh_i, nor_6_out, _74138_3_pin9);
  or or_14 (pBl_i, nor_6_out, _74138_3_pin7);
  or or_15 (pAc_plus__plus, nor_6_out, _74138_4_pin9);
  or or_16 (or_16_out, nor_6_out, _74138_2_pin15);
  or or_17 (or_17_out, nor_5_out, _74138_2_pin7);
  and and_15 (pBc_a, or_9_out, or_10_out);
  and and_16 (pAc_a, or_16_out, or_17_out);

  assign DBG[3:0] = ALU_op;
  assign NC = 1'b0;

  // Notes on the sheet:
  //   DATA: default 191
  //   CONTROL_low loads microcode_0.bin.hex
  //   CONTROL_high loads microcode_1.bin.hex
endmodule
